# Fritzing sketch schematics (saved by Fritzing 0.9.3b)

parts:
  Part1 = Arduino Nano (Rev3.0)
  M1 = fc-51 [package=THT]
  A1 = HC-SR501 Body Sensor Module
  DFRobot_DFPlayer_Mini1 = DFRobot DFPlayer Mini [part_number=DFR0299]
  SP1 = SPEAKER [package=pcb_mount_speaker]
  M3 = DC Motor
  M2 = DC Motor
  U1 = 2-Channel 5v Relay Shield [package=relay-2ch5v10a]
  LED1 = smd LED [color="Red (633nm)" package="0805 [SMD]"]
  R1 = Resistor [tolerance=±5% resistance=220 package="0402 [SMD]"]
  A2 = HC-SR501 Body Sensor Module
  IC1 = IC, DIP package, 8 pins [chip_label=IC]
  JP1 = Header 10 [package=1x10-2mm-smd]

nets:
  N1: Part1.D2, U1.IN2
  N2: Part1.D3, U1.IN1
  N3: Part1.D10, DFRobot_DFPlayer_Mini1.TX
  N4: Part1.D11/MOSI, DFRobot_DFPlayer_Mini1.RX
  N5: Part1.A3, R1.Pin_1, JP1.4
  N6: Part1.A2, A2.OUT
  N7: Part1.A1, A1.OUT
  N8: Part1.A0, M1.pin1
  N9: DFRobot_DFPlayer_Mini1.SPK_1, SP1.-, JP1.2
  N10: DFRobot_DFPlayer_Mini1.SPK_2, SP1.+, JP1.1
  N11: M3.pin_2, U1.K2-On
  N12: M2.pin_1, IC1.pin4
  N13: M2.pin_2, IC1.pin3
  N14: U1.K1-In, IC1.pin5, JP1.6
  N15: U1.K1-On, IC1.pin6, JP1.7
  N16: LED1.cathode, JP1.3
  N17: LED1.anode, R1.Pin_0
  N18: IC1.pin1, JP1.10
  N19: IC1.pin7, JP1.8
  N20: IC1.pin8, JP1.9

notes:
  soap pump
  coocoo
  IR sensor
  Shake Sensor Analog
  CooCoo logic
  coocoo trigger
  1,5V + 3,3V

custom parts:
  HC-SR501 Body Sensor Module: Pyroelectric Infrared PIR Motion Sensor Detector Module
  2-Channel 5v Relay Shield: 2 Channel 5v Relay Shield w. 2x SPD-06VDC-SD-C
